# Fritzing sketch Button+LED (saved by Fritzing 1.0.4)
breadboards: 1

parts:
  Part1 = Arduino Uno (Rev3)
  S7 = Pushbutton [package="[THT]"]
  R1 = Resistor [tolerance=±5% resistance=220 package="0603 [SMD]"]
  LED1 = smd LED [color="Red (633nm)" package="0603 [SMD]"]

nets:
  N1: Part1.D2, S7.Pin_1, S7.Pin_2
  N2: Part1.GND, S7.Pin_3, S7.Pin_4, LED1.cathode
  N3: R1.Pin_0, LED1.anode
